// Digital circuit 3bit ALU.dig as structural Verilog
module _3bit_ALU (
  input  [2:0] A_2_0,
  input  [2:0] B_2_0,
  input  [1:0] OP_1_0,
  output [2:0] O_2_0,
  output CF
);

  wire [2:0] _3bit_adder_1_o_2_0, _3bit_not_1_o_2_0, _3bit_shift_right_1_o_2_0;

  _3bit_Adder _3bit_adder_1 (.A_2_0(A_2_0), .B_2_0(B_2_0), .O_2_0(_3bit_adder_1_o_2_0), .Cout(CF));
  _3bit_NOT _3bit_not_1 (.A_2_0(A_2_0), .O_2_0(_3bit_not_1_o_2_0));
  _3bit_Shift_Right _3bit_shift_right_1 (.A_2_0(A_2_0), .B_2_0(B_2_0), .O_2_0(_3bit_shift_right_1_o_2_0));
  Multiplexer #(.Selector_Bits(2), .Bits(3)) multiplexer_1 (
    .sel(OP_1_0), .in_0(_3bit_adder_1_o_2_0), .in_1(_3bit_not_1_o_2_0), .in_2(_3bit_shift_right_1_o_2_0),
    .in_3(3'b000), .out(O_2_0));

  // Other names for the same wires on the sheet: A[2:0] = A_2_0; B[2:0] = B_2_0
endmodule
