// Digital circuit 4bit Program Counter.dig as structural Verilog
module _4bit_Program_Counter (
  input  CLK,
  input  [3:0] I_3_0,
  output [3:0] O_3_0
);

  _1bit_Reg _1bit_reg_1 (.Dout(O_3_0[0]), .Din(I_3_0[0]), .Sel(1'b1), .CLK(CLK));
  _3bit_Reg _3bit_reg_1 (.Din_2_0(I_3_0[3:1]), .Sel(1'b1), .CLK(CLK), .Dout_2_0(O_3_0[3:1]));

  // Other names for the same wires on the sheet: B0 = O_3_0[0]; B1[2:0] = O_3_0[3:1]; A0 = I_3_0[0];
  //   A1[2:0] = I_3_0[3:1]
endmodule
