// Digital circuit Control_Unit.dig as structural Verilog
module Control_Unit (
  input  [3:0] Opcode_3_0,
  input  CF,
  output [1:0] Op_1_0,
  output Reg_EN,
  output Imm_Sel,
  output JMP_Sel
);

  wire and_1_out, and_3_out, and_4_out, and_5_out, or_2_out;

  and and_1 (and_1_out, ~Opcode_3_0[2], ~Opcode_3_0[3]);  // And
  and and_2 (Imm_Sel, Opcode_3_0[2], ~Opcode_3_0[3]);  // And
  and and_3 (and_3_out, ~Opcode_3_0[2], Opcode_3_0[3]);  // And
  and and_4 (and_4_out, ~Opcode_3_0[0], ~Opcode_3_0[1]);  // And
  and and_5 (and_5_out, Opcode_3_0[0], ~Opcode_3_0[1], CF);  // And
  or or_1 (Reg_EN, and_1_out, Imm_Sel);
  or or_2 (or_2_out, and_4_out, and_5_out);
  and and_6 (JMP_Sel, and_3_out, or_2_out);

  assign Op_1_0 = Opcode_3_0[1:0];
endmodule
