// Digital circuit 9X17 RAM.dig as structural Verilog
module _9X17_RAM (
  input  [3:0] WA_3_0,
  input  WE,
  input  CLK,
  input  [3:0] RA1_3_0,
  input  [3:0] RA2_3_0,
  input  [16:0] WRD_16_0,
  output [16:0] RD1_16_0,
  output [16:0] RD2_16_0
);

  wire RA1_0, RA1_1, RA1_2, RA1_3, RA1_4, RA1_5, RA1_6, RA1_7, RA1_8, RA2_0, RA2_1, RA2_2, RA2_3, RA2_4,
       RA2_5, RA2_6, RA2_7, RA2_8, W0, W1, W2, W3, W4, W5, W6, W7, W8, WS0, WS1, WS2, WS3, WS4, WS5, WS6,
       WS7, WS8;
  wire [16:0] or_1_out, or_2_out, or_3_out, or_4_out, RD1_0, RD1_1, RD1_2, RD1_3, RD1_4, RD1_5, RD1_6, RD1_7,
       RD1_8, RD2_0, RD2_1, RD2_2, RD2_3, RD2_4, RD2_5, RD2_6, RD2_7, RD2_8;

  and and_1 (WS0, W0, WE);
  and and_2 (WS3, W3, WE);
  and and_3 (WS6, W6, WE);
  Decoder #(.Selector_Bits(4)) decoder_1 (
    .sel(RA1_3_0), .out_0(RA1_0), .out_1(RA1_1), .out_2(RA1_2), .out_3(RA1_3), .out_4(RA1_4), .out_5(RA1_5),
    .out_6(RA1_6), .out_7(RA1_7), .out_8(RA1_8));  // open: out_9, out_10, out_11, out_12, out_13, out_14, out_15
  Decoder #(.Selector_Bits(4)) decoder_2 (
    .sel(WA_3_0), .out_0(W0), .out_1(W1), .out_2(W2), .out_3(W3), .out_4(W4), .out_5(W5), .out_6(W6),
    .out_7(W7), .out_8(W8));  // open: out_9, out_10, out_11, out_12, out_13, out_14, out_15
  and and_4 (WS1, W1, WE);
  and and_5 (WS4, W4, WE);
  and and_6 (WS7, W7, WE);
  Decoder #(.Selector_Bits(4)) decoder_3 (
    .sel(RA2_3_0), .out_0(RA2_0), .out_1(RA2_1), .out_2(RA2_2), .out_3(RA2_3), .out_4(RA2_4), .out_5(RA2_5),
    .out_6(RA2_6), .out_7(RA2_7), .out_8(RA2_8));  // open: out_9, out_10, out_11, out_12, out_13, out_14, out_15
  and and_7 (WS2, W2, WE);
  and and_8 (WS5, W5, WE);
  and and_9 (WS8, W8, WE);
  _1X17_RAM _1x17_ram_1 (
    .RS1(RA1_8), .RS2(RA2_8), .WS(WS8), .WD_16_0(WRD_16_0), .CLK(CLK), .RD1_16_0(RD1_8), .RD2_16_0(RD2_8));
  _1X17_RAM _1x17_ram_2 (
    .RS1(RA1_7), .RS2(RA2_7), .WS(WS7), .WD_16_0(WRD_16_0), .CLK(CLK), .RD1_16_0(RD1_7), .RD2_16_0(RD2_7));
  _1X17_RAM _1x17_ram_3 (
    .RS1(RA1_6), .RS2(RA2_6), .WS(WS6), .WD_16_0(WRD_16_0), .CLK(CLK), .RD1_16_0(RD1_6), .RD2_16_0(RD2_6));
  _1X17_RAM _1x17_ram_4 (
    .RS1(RA1_5), .RS2(RA2_5), .WS(WS5), .WD_16_0(WRD_16_0), .CLK(CLK), .RD1_16_0(RD1_5), .RD2_16_0(RD2_5));
  _1X17_RAM _1x17_ram_5 (
    .RS1(RA1_4), .RS2(RA2_4), .WS(WS4), .WD_16_0(WRD_16_0), .CLK(CLK), .RD1_16_0(RD1_4), .RD2_16_0(RD2_4));
  _1X17_RAM _1x17_ram_6 (
    .RS1(RA1_3), .RS2(RA2_3), .WS(WS3), .WD_16_0(WRD_16_0), .CLK(CLK), .RD1_16_0(RD1_3), .RD2_16_0(RD2_3));
  _1X17_RAM _1x17_ram_7 (
    .RS1(RA1_2), .RS2(RA2_2), .WS(WS2), .WD_16_0(WRD_16_0), .CLK(CLK), .RD1_16_0(RD1_2), .RD2_16_0(RD2_2));
  _1X17_RAM _1x17_ram_8 (
    .RS1(RA1_1), .RS2(RA2_1), .WS(WS1), .WD_16_0(WRD_16_0), .CLK(CLK), .RD1_16_0(RD1_1), .RD2_16_0(RD2_1));
  _1X17_RAM _1x17_ram_9 (
    .RS1(RA1_0), .RS2(RA2_0), .WS(WS0), .WD_16_0(WRD_16_0), .CLK(CLK), .RD1_16_0(RD1_0), .RD2_16_0(RD2_0));
  assign or_1_out = RD1_8 | RD1_7 | RD1_6 | RD1_5;  // Or or_1, 17 bits wide
  assign or_2_out = RD1_4 | RD1_3 | RD1_2 | RD1_1;  // Or or_2, 17 bits wide
  assign or_3_out = RD2_8 | RD2_7 | RD2_6 | RD2_5;  // Or or_3, 17 bits wide
  assign or_4_out = RD2_4 | RD2_3 | RD2_2 | RD2_1;  // Or or_4, 17 bits wide
  assign RD1_16_0 = or_1_out | or_2_out | RD1_0;  // Or or_5, 17 bits wide
  assign RD2_16_0 = or_3_out | or_4_out | RD2_0;  // Or or_6, 17 bits wide

  // Other names for the same wires on the sheet: WRD[16:0] = WRD_16_0
endmodule
