// Digital circuit 3bit_Reg.dig as structural Verilog
module _3bit_Reg (
  input  Sel,
  input  CLK,
  input  [2:0] Din_2_0,
  output [2:0] Dout_2_0
);

  _1bit_Reg _1bit_reg_1 (.Dout(Dout_2_0[2]), .Din(Din_2_0[2]), .Sel(Sel), .CLK(CLK));
  _1bit_Reg _1bit_reg_2 (.Dout(Dout_2_0[1]), .Din(Din_2_0[1]), .Sel(Sel), .CLK(CLK));
  _1bit_Reg _1bit_reg_3 (.Dout(Dout_2_0[0]), .Din(Din_2_0[0]), .Sel(Sel), .CLK(CLK));

  // Other names for the same wires on the sheet: B0 = Dout_2_0[0]; B1 = Dout_2_0[1]; B2 = Dout_2_0[2];
  //   A0 = Din_2_0[0]; A1 = Din_2_0[1]; A2 = Din_2_0[2]
endmodule
